// Logisim project control_logic.circ as structural Verilog: 1 circuit, main circuit control_logic
module control_logic (
  input  [31:0] inst,
  input  BrEq,
  input  BrLt,
  output PCSel,
  output RegWEn,
  output [2:0] ImmSel,
  output BrUn,
  output ASel,
  output BSel,
  output [3:0] ALUSel,
  output MemRW,
  output [1:0] WBSel,
  output CSRSel,
  output CSRWen
);

  wire and_4_out, and_5_out, and_6_out, comparator_1_eq, comparator_2_eq, comparator_3_eq, comparator_4_eq,
       comparator_5_eq, comparator_6_eq, comparator_7_eq, comparator_8_eq, comparator_9_eq, comparator_10_eq,
       comparator_11_eq, comparator_12_eq, comparator_13_eq, comparator_14_eq, isAuipc, isCsr, isIType,
       isJalr, isLui, isLw, isMul, isMulh, isMulhu, isRType, isSBType, isSra, isSType, isSub, isUJType,
       not_1_out, not_2_out, not_3_out, not_4_out, not_5_out, not_6_out, not_7_out, not_8_out, not_9_out,
       not_10_out, not_11_out, not_12_out, not_13_out, not_14_out, not_15_out, not_16_out, not_17_out,
       not_18_out, not_19_out, not_20_out, not_21_out, not_22_out, not_23_out, not_24_out, not_25_out,
       not_26_out, not_27_out, not_28_out, not_29_out, not_30_out, or_1_out, or_4_out;
  wire [3:0] multiplexer_1_out, multiplexer_2_out, multiplexer_3_out, multiplexer_4_out, multiplexer_5_out,
       multiplexer_7_out, RISel;

  not not_1 (not_1_out, inst[6]);
  not not_2 (not_2_out, inst[3]);
  not not_3 (not_3_out, inst[2]);
  not not_4 (not_4_out, inst[6]);
  not not_5 (not_5_out, inst[5]);
  and and_1 (isRType, not_1_out, inst[5], inst[4], not_2_out, not_3_out, inst[1], inst[0]);
  Comparator #(.width(3)) comparator_1 (.a(inst[14:12]), .b(3'b100), .eq(comparator_1_eq));  // open: gt, lt
  Comparator #(.width(3)) comparator_2 (.a(inst[14:12]), .b(3'b110), .eq(comparator_2_eq));  // open: gt, lt
  not not_6 (not_6_out, inst[3]);
  not not_7 (not_7_out, inst[2]);
  not not_8 (not_8_out, inst[6]);
  not not_9 (not_9_out, inst[5]);
  not not_10 (not_10_out, inst[4]);
  and and_2 (isIType, not_4_out, not_5_out, inst[4], not_6_out, not_7_out, inst[1], inst[0]);
  Comparator #(.width(3)) comparator_3 (.a(inst[14:12]), .b(3'b000), .eq(comparator_3_eq));  // open: gt, lt
  not not_11 (not_11_out, BrEq);
  Comparator #(.width(3)) comparator_4 (.a(inst[14:12]), .b(3'b001), .eq(comparator_4_eq));  // open: gt, lt
  or or_1 (or_1_out, comparator_1_eq, comparator_2_eq);
  not not_12 (not_12_out, inst[3]);
  not not_13 (not_13_out, inst[2]);
  not not_14 (not_14_out, inst[6]);
  not not_15 (not_15_out, inst[4]);
  and and_3 (isLw, not_8_out, not_9_out, not_10_out, not_12_out, not_13_out, inst[1], inst[0]);
  and and_4 (and_4_out, isSBType, BrEq, comparator_3_eq);
  and and_5 (and_5_out, isSBType, not_11_out, comparator_4_eq);
  and and_6 (and_6_out, isSBType, BrLt, or_1_out);
  not not_16 (not_16_out, inst[3]);
  not not_17 (not_17_out, inst[2]);
  not not_18 (not_18_out, inst[4]);
  and and_7 (isSType, not_14_out, inst[5], not_15_out, not_16_out, not_17_out, inst[1], inst[0]);
  not not_19 (not_19_out, inst[3]);
  not not_20 (not_20_out, inst[2]);
  not not_21 (not_21_out, inst[6]);
  not not_22 (not_22_out, inst[5]);
  and and_8 (isSBType, inst[6], inst[5], not_18_out, not_19_out, not_20_out, inst[1], inst[0]);
  or or_2 (PCSel, and_4_out, and_5_out, and_6_out, isUJType, isJalr);
  not not_23 (not_23_out, inst[3]);
  not not_24 (not_24_out, inst[6]);
  and and_9 (isAuipc, not_21_out, not_22_out, inst[4], not_23_out, inst[2], inst[1], inst[0]);
  not not_25 (not_25_out, inst[4]);
  not not_26 (not_26_out, inst[3]);
  and and_10 (isLui, not_24_out, inst[5], inst[4], not_26_out, inst[2], inst[1], inst[0]);
  not not_27 (not_27_out, inst[4]);
  and and_11 (isUJType, inst[6], inst[5], not_25_out, inst[3], inst[2], inst[1], inst[0]);
  not not_28 (not_28_out, inst[3]);
  and and_12 (isJalr, inst[6], inst[5], not_27_out, not_28_out, inst[2], inst[1], inst[0]);
  or or_3 (RegWEn, isRType, isIType, isLw, isAuipc, isLui, isCsr);
  not not_29 (not_29_out, inst[3]);
  not not_30 (not_30_out, inst[2]);
  and and_13 (isCsr, inst[6], inst[5], inst[4], not_29_out, not_30_out, inst[1], inst[0]);
  Multiplexer #(.enable("false"), .select(3), .width(4)) multiplexer_1 (
    .in0(4'b0000), .in1(4'b0110), .in2(4'b0111), .in4(4'b0011), .in5(4'b0100), .in6(4'b0010), .in7(4'b0001),
    .out(multiplexer_1_out), .sel(inst[14:12]));  // open: in3
  Comparator #(.width(3)) comparator_5 (.a(inst[14:12]), .b(3'b000), .eq(comparator_5_eq));  // open: gt, lt
  Comparator #(.width(7)) comparator_6 (.a(inst[31:25]), .b(7'b0000001), .eq(comparator_6_eq));  // open: gt, lt
  Comparator #(.width(3)) comparator_7 (.a(inst[14:12]), .b(3'b000), .eq(comparator_7_eq));  // open: gt, lt
  Comparator #(.width(7)) comparator_8 (.a(inst[31:25]), .b(7'b0100000), .eq(comparator_8_eq));  // open: gt, lt
  Comparator #(.width(3)) comparator_9 (.a(inst[14:12]), .b(3'b001), .eq(comparator_9_eq));  // open: gt, lt
  Comparator #(.width(7)) comparator_10 (.a(inst[31:25]), .b(7'b0000001), .eq(comparator_10_eq));  // open: gt, lt
  and and_14 (isMul, isRType, comparator_5_eq, comparator_6_eq);
  and and_15 (isSub, isRType, comparator_7_eq, comparator_8_eq);
  and and_16 (isMulh, isRType, comparator_9_eq, comparator_10_eq);
  Multiplexer #(.enable("false"), .width(4)) multiplexer_2 (
    .in0(multiplexer_1_out), .in1(4'b1010), .out(multiplexer_2_out), .sel(isMul));
  Multiplexer #(.enable("false"), .width(4)) multiplexer_3 (
    .in0(multiplexer_2_out), .in1(4'b1011), .out(multiplexer_3_out), .sel(isMulhu));
  Multiplexer #(.enable("false"), .width(4)) multiplexer_4 (
    .in0(multiplexer_3_out), .in1(4'b1100), .out(multiplexer_4_out), .sel(isSub));
  Multiplexer #(.enable("false"), .width(4)) multiplexer_5 (
    .in0(multiplexer_4_out), .in1(4'b1110), .out(multiplexer_5_out), .sel(isMulh));
  Comparator #(.width(3)) comparator_11 (.a(inst[14:12]), .b(3'b011), .eq(comparator_11_eq));  // open: gt, lt
  Multiplexer #(.enable("false"), .width(4)) multiplexer_6 (
    .in0(multiplexer_5_out), .in1(4'b0101), .out(RISel), .sel(isSra));
  Comparator #(.width(7)) comparator_12 (.a(inst[31:25]), .b(7'b0000001), .eq(comparator_12_eq));  // open: gt, lt
  Comparator #(.width(3)) comparator_13 (.a(inst[14:12]), .b(3'b101), .eq(comparator_13_eq));  // open: gt, lt
  Comparator #(.width(7)) comparator_14 (.a(inst[31:25]), .b(7'b0100000), .eq(comparator_14_eq));  // open: gt, lt
  and and_17 (isMulhu, isRType, comparator_11_eq, comparator_12_eq);
  and and_18 (isSra, comparator_13_eq, comparator_14_eq);
  or or_4 (or_4_out, isRType, isIType);
  Multiplexer #(.enable("false"), .width(4)) multiplexer_7 (
    .in0(4'b0000), .in1(RISel), .out(multiplexer_7_out), .sel(or_4_out));
  Multiplexer #(.enable("false"), .width(4)) multiplexer_8 (
    .in0(multiplexer_7_out), .in1(4'b1100), .out(ALUSel), .sel(isSBType));

  // Other names for the same wires on the sheet: opcode[6:0] = inst[6:0]; opcode0 = inst[0]; opcode1 = inst[1];
  //   opcode2 = inst[2]; opcode3 = inst[3]; opcode4 = inst[4]; opcode5 = inst[5]; opcode6 = inst[6];
  //   funct3[2:0] = inst[14:12]; funct3_0 = inst[12]; funct3_1 = inst[13]; funct3_2 = inst[14];
  //   funct7[6:0] = inst[31:25]; funct7_0 = inst[25]; funct7_5 = inst[30]

  // Notes on the sheet:
  //   INPUTS to your circuit
  //   产生PCSel
  //   DON'T CHANGE THE LOCATIONS OF THE INPUTS AND OUTPUTS!
  //   OUTPUT from your circuit
  //   一级译码
  //   产生RegWEn
  //   add
  //   sll
  //   slt
  //   xor
  //   srl
  //   or
  //   and
  //   产生ImmSel
  //   二级译码
  //   产生ALUSel
endmodule
